// Logisim project DMux4Way.circ as structural Verilog: 1 circuit, main circuit main
module main (
  input  Inp,
  input  Sel0,
  input  Sel1,
  input  S0,
  input  S1,
  input  InpData,
  output out_7,
  output out_8,
  output out_9,
  output out_10,
  output a,
  output b,
  output c,
  output d
);

  wire demultiplexer_1_out0, demultiplexer_1_out1, not_1_out, not_2_out;

  Demultiplexer demultiplexer_1 (.out0(demultiplexer_1_out0), .out1(demultiplexer_1_out1), .in(Inp), .sel(Sel0));
  not not_1 (not_1_out, S0);
  not not_2 (not_2_out, S1);
  Demultiplexer demultiplexer_2 (.out0(out_7), .out1(out_8), .in(demultiplexer_1_out0), .sel(Sel1));
  Demultiplexer demultiplexer_3 (.out0(out_9), .out1(out_10), .in(demultiplexer_1_out1), .sel(Sel1));
  and and_1 (a, InpData, not_1_out, not_2_out);
  and and_2 (b, InpData, not_1_out, S1);
  and and_3 (c, InpData, S0, not_2_out);
  and and_4 (d, InpData, S0, S1);
endmodule
