// Logisim project my.circ as structural Verilog: 1 circuit, main circuit main
module main (
  input  set,
  input  reset,
  input  in_3,
  input  in_4,
  input  in_5,
  input  in_6,
  input  [15:0] inputt,
  input  Load,
  input  [2:0] Addresss,
  output out_10,
  output out_11,
  output Q_out,
  output out_13,
  output Q,
  output Qcomplement,
  output [15:0] Out_put
);

  wire and_1_out, and_2_out, clock_1_out, demultiplexer_1_out0, not_1_out, not_2_out, not_3_out;
  wire [15:0] multiplexer_1_out, multiplexer_2_out, r0_q, r1_q, r2_q, r3_q, r4_q, r5_q, r6_q, r7_q;

  Multiplexer #(.width(16)) multiplexer_1 (
    .in0(Out_put), .in1(inputt), .out(multiplexer_1_out), .sel(demultiplexer_1_out0));
  nor nor_1 (out_11, set, out_10);
  nor nor_2 (out_10, out_11, reset);
  not not_1 (not_1_out, not_3_out);
  nor nor_3 (Q_out, in_3, out_13);
  nor nor_4 (out_13, Q_out, in_4);
  not not_2 (not_2_out, in_5);
  Clock clock_1 (.out(clock_1_out));
  not not_3 (not_3_out, not_1_out);
  and and_1 (and_1_out, in_5, in_6);
  and and_2 (and_2_out, in_6, not_2_out);
  Register #(.width(16)) r0 (
    .D(multiplexer_1_out), .en(demultiplexer_1_out0), .clk(clock_1_out), .Q(r0_q));  // open: clr
  Register #(.width(16)) r1 (.Q(r1_q));  // open: D, en, clk, clr
  Register #(.width(16)) r2 (.Q(r2_q));  // open: D, en, clk, clr
  Register #(.width(16)) r3 (.Q(r3_q));  // open: D, en, clk, clr
  Register #(.width(16)) r4 (.Q(r4_q));  // open: D, en, clk, clr
  Register #(.width(16)) r5 (.Q(r5_q));  // open: D, en, clk, clr
  Register #(.width(16)) r6 (.Q(r6_q));  // open: D, en, clk, clr
  Register #(.width(16)) r7 (.Q(r7_q));  // open: D, en, clk, clr
  nor nor_5 (Q, and_1_out, Qcomplement);
  nor nor_6 (Qcomplement, Q, and_2_out);
  Multiplexer #(.select(3), .width(16)) multiplexer_2 (
    .in0(r0_q), .in1(r1_q), .in2(r2_q), .in3(r3_q), .in4(r4_q), .in5(r5_q), .in6(r6_q), .in7(r7_q),
    .out(multiplexer_2_out), .sel(Addresss));
  Multiplexer #(.width(16)) multiplexer_3 (.in0(multiplexer_2_out), .in1(inputt), .out(Out_put), .sel(Load));
  Demultiplexer #(.select(3)) demultiplexer_1 (
    .out0(demultiplexer_1_out0), .in(Load), .sel(Addresss));  // open: out1, out2, out3, out4, out5, out6, out7
endmodule
